# Fritzing sketch electronics-from_arduino_to_pump (saved by Fritzing 0.9.10b)
breadboards: 1

parts:
  R2 = Resistor [tolerance=±5% power=0.25 resistance=560 package=THT]
  Part1 = Arduino Uno (Rev3)
  C1 = Electrolytic Capacitor [capacitance=1µF voltage=35V package="100 mil [THT, electrolytic]"]
  U1 = mystery part, 4 pins [chip_label="Pump controller"]

nets:
  N1: R2.Pin_0, C1.+, U1.pin1
  N2: R2.Pin_1, Part1.D6_PWM
  N3: Part1.D12/MISO, U1.pin3
  N4: Part1.D13/SCK, U1.pin2
  N5: Part1.GND, C1.-, U1.pin4
