# Fritzing sketch electronics-from_printer_to_arduino (saved by Fritzing 0.9.10b)
breadboards: 1

parts:
  R1 = Resistor [tolerance=±5% power=0.25 resistance=22k package=THT]
  D1 = Rectifier Diode [part_number=1N4001 package="300 mil [THT]"]
  R2 = Resistor [tolerance=±5% power=0.25 resistance=1k package=THT]
  Part1 = Arduino Uno (Rev3)
  C1 = Ceramic Capacitor [capacitance=100nF voltage=35V package="100 mil [THT, multilayer]"]
  U1 = mystery part, 4 pins [chip_label="Stepper controller"]

nets:
  N1: R1.Pin_0, U1.pin2
  N2: R1.Pin_1, R2.Pin_1, Part1.A0, C1.1
  N3: D1.cathode, U1.pin1
  N4: D1.anode, R2.Pin_0, Part1.GND, C1.0
