# Fritzing sketch electronics-invert_switch (saved by Fritzing 0.9.10b)
breadboards: 1

parts:
  R1 = Resistor [tolerance=±5% power=0.25 resistance=22k package=THT]
  Part1 = Arduino Uno (Rev3)
  S2 = SWITCH-MOMENTARY-2 [package=tactile_switch_smd-2]

nets:
  N1: R1.Pin_0, Part1.GND
  N2: R1.Pin_1, Part1.D8, S2.2
  N3: Part1.5V, S2.1
